# Fritzing sketch SensoriamentoFirebase (saved by Fritzing 0.9.3b)
breadboards: 1

parts:
  U1 = NodeMCU V1.0
  RHT1 = Humidity and Temperature Sensor RHT03
  Componente1 = HC-SR501 Body Sensor Module
  R1 = Resistor [tolerance=±5% resistance=100 package="0402 [SMD]"]
  LED1 = smd LED [color="Green (555nm)" package="1206 [SMD]"]
  R4 = Resistor [tolerance=±5% resistance=10k package=THT]

nets:
  N1: U1.D3, R1.Pin_1
  3V3: U1.3V3, RHT1.Vcc, R4.Pin_1
  GND: U1.GND, RHT1.GND_1, Componente1.GND, LED1.cathode
  N2: U1.D5, RHT1.Data-signal, R4.Pin_0
  N3: U1.D6, Componente1.OUT
  VIN: U1.Vin, Componente1.VCC

notes:
  3.3v
  DHT11
  10k
  100ohm

custom parts:
  NodeMCU V1.0: ESP8266 based NodeMCU
  HC-SR501 Body Sensor Module: Pyroelectric Infrared PIR Motion Sensor Detector Module
